// Digital circuit lab_1.dig as structural Verilog
module lab_1 (
  input  X,
  input  Y,
  input  Z,
  input  X_2,
  input  Y_2,
  input  Z_2,
  output X__plus__YZ,
  output X_plus_Y___X_plus_Z
);

  wire and_1_out, or_1_out, or_2_out;

  and and_1 (and_1_out, Y, Z);
  or or_1 (or_1_out, X_2, Y_2);
  or or_2 (or_2_out, X_2, Z_2);
  or or_3 (X__plus__YZ, X, and_1_out);
  and and_2 (X_plus_Y___X_plus_Z, or_1_out, or_2_out);
endmodule
