// Digital circuit developedoct2seven.dig as structural Verilog
module developedoct2seven (
  input  d2,
  input  d1,
  input  d0,
  output a,
  output b,
  output c,
  output d,
  output e,
  output f,
  output g
);

  wire and_1_out, and_2_out, and_3_out, and_4_out, and_5_out, and_6_out, and_7_out, and_8_out, and_9_out,
       and_10_out, and_11_out, and_12_out, and_13_out, and_14_out, and_15_out, and_16_out, not_1_out,
       not_2_out, not_3_out, or_1_out, or_2_out, or_3_out, or_4_out, or_5_out, or_7_out, or_8_out, or_11_out,
       or_12_out;

  not not_1 (not_1_out, d2);
  not not_2 (not_2_out, d1);
  not not_3 (not_3_out, d0);
  and and_1 (and_1_out, not_2_out, d2);
  and and_2 (and_2_out, not_1_out, d1);
  and and_3 (and_3_out, not_3_out, not_1_out);
  and and_4 (and_4_out, d1, not_3_out);
  or or_1 (or_1_out, d1, not_1_out);
  and and_5 (and_5_out, not_3_out, not_2_out);
  and and_6 (and_6_out, not_2_out, d2);
  and and_7 (and_7_out, d2, not_3_out);
  and and_8 (and_8_out, not_1_out, d1);
  and and_9 (and_9_out, d1, not_3_out);
  and and_10 (and_10_out, not_3_out, d2);
  and and_11 (and_11_out, d2, not_2_out);
  and and_12 (and_12_out, d0, d2);
  and and_13 (and_13_out, not_3_out, not_1_out);
  and and_14 (and_14_out, not_3_out, not_2_out);
  and and_15 (and_15_out, d0, d1);
  or or_2 (or_2_out, not_2_out, d2);
  or or_3 (or_3_out, and_14_out, and_15_out);
  or or_4 (or_4_out, and_8_out, and_9_out);
  or or_5 (or_5_out, and_10_out, and_11_out);
  or or_6 (c, d0, or_2_out);
  and and_16 (and_16_out, d0, and_1_out);
  and and_17 (e, not_3_out, or_1_out);
  or or_7 (or_7_out, and_5_out, and_6_out);
  or or_8 (or_8_out, and_12_out, d1);
  or or_9 (g, or_4_out, or_5_out);
  or or_10 (b, or_3_out, not_1_out);
  or or_11 (or_11_out, and_16_out, and_2_out);
  or or_12 (or_12_out, and_3_out, and_4_out);
  or or_13 (f, or_7_out, and_7_out);
  or or_14 (a, or_8_out, and_13_out);
  or or_15 (d, or_11_out, or_12_out);
endmodule
