// Digital circuit absmodified.dig as structural Verilog
module absmodified (
  input  A2,
  input  A1,
  input  A0,
  input  input_zero,
  output ABS2,
  output ABS1,
  output ABS0,
  output sign,
  output not_needed
);

  wire and_1_out, and_2_out, and_3_out, and_4_out, and_5_out, and_6_out, or_1_out, or_2_out, xor_1_out,
       xor_2_out, xor_3_out, xor_4_out, xor_5_out, xor_6_out;

  xor xor_1 (xor_1_out, A2, A2);
  xor xor_2 (xor_2_out, A2, A1);
  xor xor_3 (xor_3_out, A2, A0);
  xor xor_4 (xor_4_out, input_zero, xor_3_out);
  and and_1 (and_1_out, input_zero, xor_3_out);
  xor xor_5 (xor_5_out, input_zero, xor_2_out);
  and and_2 (and_2_out, input_zero, xor_2_out);
  xor xor_6 (xor_6_out, input_zero, xor_1_out);
  and and_3 (and_3_out, input_zero, xor_1_out);
  xor xor_7 (ABS0, xor_4_out, A2);
  and and_4 (and_4_out, xor_4_out, A2);
  xor xor_8 (ABS1, xor_5_out, or_1_out);
  and and_5 (and_5_out, xor_5_out, or_1_out);
  xor xor_9 (ABS2, xor_6_out, or_2_out);
  and and_6 (and_6_out, xor_6_out, or_2_out);
  or or_1 (or_1_out, and_4_out, and_1_out);
  or or_2 (or_2_out, and_5_out, and_2_out);
  or or_3 (not_needed, and_6_out, and_3_out);

  assign sign = A2;
  // also tied to GND on the sheet: input_zero
endmodule
