// Digital circuit controller.dig as structural Verilog
module controller (
  input  clk,
  input  UP,
  input  DOWN,
  output [3:0] cnt
);

  wire and_1_out, and_2_out, not_1_out, not_2_out, not_3_out, or_1_out, prevDOWN_q, prevUP_q, updown_1_p1,
       updown_1_p2;

  D_FF prevUP (.D(UP), .C(clk), .Q(prevUP_q));  // open: nQ
  D_FF prevDOWN (.D(DOWN), .C(clk), .Q(prevDOWN_q));  // open: nQ
  not not_1 (not_1_out, prevUP_q);
  not not_2 (not_2_out, prevDOWN_q);
  and and_1 (and_1_out, UP, not_1_out);
  and and_2 (and_2_out, DOWN, not_2_out);
  or or_1 (or_1_out, and_1_out, and_2_out);
  not not_3 (not_3_out, and_1_out);
  // updown updown_1: pin names not known; wires that end beside it: updown_1_p1, updown_1_p2, clk, cnt
  and and_3 (updown_1_p1, and_1_out, or_1_out);
  and and_4 (updown_1_p2, not_3_out, or_1_out);
endmodule
