// Digital circuit lfsrfinal.dig as structural Verilog
module lfsrfinal (
  input  CLK,
  output [2:0] bit_out
);

  wire Q0_q, Q1_q, Q2_q, Q3_q, Q4_q, Q5_q, Q6_q, Q7_q, Q8_q, Q9_q, Q10_q, Q11_q, Q12_q, Q13_q, Q14_q, Q15_q,
       xor_1_out, xor_2_out, xor_3_out, xor_4_out, xor_5_out, xor_6_out, xor_7_out, xor_8_out, xor_9_out;

  D_FF Q15 (.D(xor_1_out), .C(CLK), .Q(Q15_q));  // open: nQ
  D_FF Q14 (.D(xor_2_out), .C(CLK), .Q(Q14_q));  // open: nQ
  D_FF Q13 (.D(xor_3_out), .C(CLK), .Q(Q13_q));  // open: nQ
  D_FF Q12 (.D(Q15_q), .C(CLK), .Q(Q12_q));  // open: nQ
  D_FF Q11 (.D(Q14_q), .C(CLK), .Q(Q11_q));  // open: nQ
  D_FF Q10 (.D(Q13_q), .C(CLK), .Q(Q10_q));  // open: nQ
  D_FF #(.Default(1)) Q9 (.D(Q12_q), .C(CLK), .Q(Q9_q));  // open: nQ
  xor xor_1 (xor_1_out, Q9_q, xor_4_out);
  D_FF #(.Default(1)) Q8 (.D(Q11_q), .C(CLK), .Q(Q8_q));  // open: nQ
  xor xor_2 (xor_2_out, Q8_q, xor_6_out);
  D_FF Q7 (.D(Q10_q), .C(CLK), .Q(Q7_q));  // open: nQ
  xor xor_3 (xor_3_out, Q7_q, xor_8_out);
  D_FF #(.Default(1)) Q6 (.D(Q9_q), .C(CLK), .Q(Q6_q));  // open: nQ
  D_FF Q5 (.D(Q8_q), .C(CLK), .Q(Q5_q));  // open: nQ
  D_FF Q4 (.D(Q7_q), .C(CLK), .Q(Q4_q));  // open: nQ
  xor xor_4 (xor_4_out, Q4_q, xor_5_out);
  D_FF Q3 (.D(Q6_q), .C(CLK), .Q(Q3_q));  // open: nQ
  xor xor_5 (xor_5_out, Q3_q, Q2_q);
  xor xor_6 (xor_6_out, Q3_q, xor_7_out);
  D_FF #(.Default(1)) Q2 (.D(Q5_q), .C(CLK), .Q(Q2_q));  // open: nQ
  xor xor_7 (xor_7_out, Q2_q, Q1_q);
  xor xor_8 (xor_8_out, Q2_q, xor_9_out);
  D_FF #(.Default(1)) Q1 (.D(Q4_q), .C(CLK), .Q(Q1_q));  // open: nQ
  xor xor_9 (xor_9_out, Q1_q, Q0_q);
  D_FF Q0 (.D(Q3_q), .C(CLK), .Q(Q0_q));  // open: nQ
  D_FF d_ff_1 (.D(Q0_q), .C(CLK), .Q(bit_out[0]));  // open: nQ
  D_FF d_ff_2 (.D(Q1_q), .C(CLK), .Q(bit_out[1]));  // open: nQ
  D_FF d_ff_3 (.D(Q2_q), .C(CLK), .Q(bit_out[2]));  // open: nQ
  Seven_Seg_Hex seven_seg_hex_1 (.d({1'b0, bit_out}), .dp(1'b0));
endmodule
