// Digital circuit labtimer.dig as structural Verilog
module labtimer (
  input  CLK,
  input  SW,
  input  B3,
  input  B2,
  input  B1,
  input  B0,
  input  HZ1,
  output [3:0] M10,
  output [3:0] M1,
  output [3:0] S10,
  output [3:0] S1
);

  wire and_1_out, and_2_out, and_3_out, and_4_out, and_5_out, and_6_out, and_7_out, and_8_out, and_9_out,
       and_10_out, and_11_out, and_12_out, and_13_out, and_14_out, comparator_1_gt, comparator_2_gt,
       comparator_3_gt, comparator_4_gt, comparator_5_eq, d_ff_1_q, d_ff_2_q, d_ff_3_q, d_ff_4_q, d_ff_5_nq,
       d_ff_6_nq, d_ff_7_nq, d_ff_8_nq, d_ff_9_nq, jk_ff_1_q, M1_ovf, multiplexer_1_out, not_1_out,
       not_2_out, not_3_out, not_4_out, not_5_out, not_6_out, or_1_out, or_2_out, or_3_out, or_4_out, S1_ovf,
       S10_ovf;

  not not_1 (not_1_out, SW);
  and and_1 (and_1_out, not_1_out, HZ1);
  not not_2 (not_2_out, B0);
  not not_3 (not_3_out, B1);
  not not_4 (not_4_out, B2);
  not not_5 (not_5_out, B3);
  D_FF d_ff_1 (.D(not_2_out), .C(CLK), .Q(d_ff_1_q));  // open: nQ
  D_FF d_ff_2 (.D(not_3_out), .C(CLK), .Q(d_ff_2_q));  // open: nQ
  D_FF d_ff_3 (.D(not_4_out), .C(CLK), .Q(d_ff_3_q));  // open: nQ
  D_FF d_ff_4 (.D(not_5_out), .C(CLK), .Q(d_ff_4_q));  // open: nQ
  D_FF d_ff_5 (.D(d_ff_1_q), .C(CLK), .nQ(d_ff_5_nq));  // open: Q
  D_FF d_ff_6 (.D(d_ff_2_q), .C(CLK), .nQ(d_ff_6_nq));  // open: Q
  D_FF d_ff_7 (.D(d_ff_3_q), .C(CLK), .nQ(d_ff_7_nq));  // open: Q
  D_FF d_ff_8 (.D(d_ff_4_q), .C(CLK), .nQ(d_ff_8_nq));  // open: Q
  and and_2 (and_2_out, d_ff_1_q, d_ff_5_nq);
  and and_3 (and_3_out, d_ff_2_q, d_ff_6_nq);
  and and_4 (and_4_out, d_ff_3_q, d_ff_7_nq);
  and and_5 (and_5_out, d_ff_4_q, d_ff_8_nq);
  not not_6 (not_6_out, SW);
  and and_6 (and_6_out, SW, and_2_out);
  and and_7 (and_7_out, SW, and_3_out);
  and and_8 (and_8_out, SW, and_4_out);
  and and_9 (and_9_out, SW, and_5_out);
  or or_1 (or_1_out, and_1_out, and_6_out);
  or or_2 (or_2_out, and_10_out, and_7_out);
  or or_3 (or_3_out, and_12_out, and_8_out);
  or or_4 (or_4_out, and_13_out, and_9_out);
  CounterPreset #(.Bits(4)) u_S1 (
    .en(or_1_out), .C(CLK), .dir(multiplexer_1_out), .in(4'b0000), .ld(1'b0), .clr(comparator_1_gt),
    .out(S1), .ovf(S1_ovf));
  CounterPreset #(.Bits(4)) u_S10 (
    .en(or_2_out), .C(CLK), .dir(multiplexer_1_out), .in(4'b0000), .ld(1'b0), .clr(comparator_2_gt),
    .out(S10), .ovf(S10_ovf));
  CounterPreset #(.Bits(4)) u_M1 (
    .en(or_3_out), .C(CLK), .dir(multiplexer_1_out), .in(4'b0000), .ld(1'b0), .clr(comparator_3_gt),
    .out(M1), .ovf(M1_ovf));
  and and_10 (and_10_out, not_6_out, S1_ovf);
  Comparator #(.Bits(4)) comparator_1 (.a(S1), .b(4'b1001), .gt(comparator_1_gt));  // open: eq, lt
  Comparator #(.Bits(4)) comparator_2 (.a(S10), .b(4'b0101), .gt(comparator_2_gt));  // open: eq, lt
  Comparator #(.Bits(4)) comparator_3 (.a(M1), .b(4'b1001), .gt(comparator_3_gt));  // open: eq, lt
  CounterPreset #(.Bits(4)) M1_2 (
    .en(or_4_out), .C(CLK), .dir(multiplexer_1_out), .in(4'b0000), .ld(1'b0), .clr(comparator_4_gt), .out(M10));  // open: ovf
  Comparator #(.Bits(4)) comparator_4 (.a(M10), .b(4'b1001), .gt(comparator_4_gt));  // open: eq, lt
  Comparator #(.Bits(16)) comparator_5 (.a({M10, M1, S10, S1}), .b({16{1'b0}}), .eq(comparator_5_eq));  // open: gt, lt
  and and_11 (and_11_out, SW, comparator_5_eq);
  and and_12 (and_12_out, S10_ovf, not_6_out);
  and and_13 (and_13_out, M1_ovf, not_6_out);
  D_FF d_ff_9 (.D(and_11_out), .C(CLK), .nQ(d_ff_9_nq));  // open: Q
  and and_14 (and_14_out, and_11_out, d_ff_9_nq);
  JK_FF jk_ff_1 (.J(and_14_out), .C(CLK), .K(and_14_out), .Q(jk_ff_1_q));  // open: nQ
  Multiplexer multiplexer_1 (.sel(SW), .in_0(jk_ff_1_q), .in_1(1'b0), .out(multiplexer_1_out));

  // Notes on the sheet:
  //   SW: default 1
endmodule
